# Fritzing sketch CurrentMirror1 (saved by Fritzing 1.0.7)
breadboards: 1

parts:
  C2 = Electrolytic Capacitor [capacitance=100pF voltage=35V package="100 mil [THT, electrolytic]"]
  C1 = Electrolytic Capacitor [capacitance=0.1mF voltage=35V package="100 mil [THT, electrolytic]"]
  RC1 = Resistor [tolerance=±5% power=0.25W resistance=1k package=THT]
  Rl1 = Resistor [tolerance=±5% power=0.25W resistance=1k package=THT]
  Q1 = PNP-Transistor [package="TO92 [THT]"]
  Q2 = NPN-Transistor [package="TO92 [THT]"]
  Q3 = PNP-Transistor [package="TO92 [THT]"]
  Q4 = NPN-Transistor [package="TO92 [THT]"]

nets:
  GND: C2.-, C1.-, Q2.E, Q4.E
  INP: C2.+, C1.+, RC1.Pin_0
  5V: RC1.Pin_1, Q1.E, Q1.B, Q2.B, Q3.E, Q3.B, Q3.C, Q4.B, Q4.C
  OUT-IN: Rl1.Pin_0
  N1: Rl1.Pin_1, Q2.C
  OUT-E: Q1.C
