# Fritzing sketch CurrentSource (saved by Fritzing 1.0.7)
breadboards: 1

parts:
  R1 = Resistor [tolerance=±5% power=0.25W resistance=100k package=THT]
  R2 = Resistor [tolerance=±5% power=0.25W resistance=100k package=THT]
  Q1 = PNP-Transistor [package="TO92 [THT]"]
  Q2 = NPN-Transistor [package="TO92 [THT]"]
  J1 = male pin header, 2 pins [form="♂ (male)"]
  J2 = male pin header, 2 pins [form="♂ (male)"]
  Q3 = P0118MA 2AL3 [part_number="P0118MA 2AL3" package="TO-92 [THT]"]
  R3 = 12mm Trimmer Potentiometer (Large) [maximum_resistance=10kΩ knob_status=50% power=0.5W package=THT]
  Q4 = PNP-Transistor [package="TO92 [THT]"]

nets:
  5V: R1.Pin_0, Q1.E, J1.pin1, Q3.G, Q4.E
  N1: R2.Pin_0, R3.leg2
  N2: R2.Pin_1, R3.leg1, R3.wiper
  N3: Q1.B, Q4.B, Q4.C
  N4: Q1.C, J2.pin1
  GND: Q2.E, J1.pin2, J2.pin2, Q3.K
  N5: Q2.B, Q3.A

custom parts:
  P0118MA 2AL3: STMicroelectronics P0118MA sensitive high-immunity SCR (thyristor) in a TO-92 through-hole package. 600 V, 0.8 A RMS on-state current, very low gate trigger current (0.5-5 µA). Order code P0118MA 2AL3 (Ammopack). Pinout (flat face forward, leads down): pin1 Anode, pin2 Cathode, pin3 Gate.
