# Fritzing sketch CurrentSource_BJT (saved by Fritzing 1.0.7)
breadboards: 1

parts:
  Q1 = PNP-Transistor [package="TO92 [THT]"]
  Q2 = PNP-Transistor [package="TO92 [THT]"]
  R2 = Resistor [tolerance=±1% power=0.25W resistance=1k package=THT]
  R6 = 6mm Trimmer Potentiometer [maximum_resistance=10kΩ knob_status=50% power=0.5W package=THT]
  Q3 = NPN-Transistor [package="TO92 [THT]"]
  R3 = Resistor [tolerance=±1% power=0.25W resistance=1k package=THT]
  R4 = Resistor [tolerance=±1% power=0.25W resistance=1k package=THT]

nets:
  N1: Q1.E, R2.Pin_0
  N2: Q1.B, Q1.C, Q2.B, Q3.C
  N3: Q2.E, R3.Pin_1
  GND: Q2.C, R4.Pin_1
  5V: R2.Pin_1, Q3.B, R3.Pin_0
  N4: R6.leg1, R6.leg2
  N5: Q3.E, R4.Pin_0
