# Fritzing sketch Delta (saved by Fritzing 1.0.7)
breadboards: 1

parts:
  R1 = Resistor [tolerance=±5% power=0.25W resistance=100k package=THT]
  R2 = Resistor [tolerance=±5% power=0.25W resistance=100k package=THT]
  R3 = Resistor [tolerance=±5% power=0.25W resistance=1k package=THT]
  R4 = Resistor [tolerance=±5% power=0.25W resistance=0 package=THT]
  R5 = 12mm Trimmer Potentiometer (Large) [maximum_resistance=10kΩ knob_status=50% power=0.5W package=THT]
  J1 = female pin header, 2 pins [form="♀ (female)"]
  Q1 = PNP-Transistor [package="TO92 [THT]"]
  Q2 = NPN-Transistor [package="TO92 [THT]"]

nets:
  5V: R1.Pin_0, Q1.E
  N1: R1.Pin_1, Q1.B, Q2.C
  INP: R2.Pin_0
  N2: R2.Pin_1, Q2.B
  GND: R3.Pin_0, J1.pin1, Q2.E
  N3: R3.Pin_1, R4.Pin_1, Q1.C
  N4: R4.Pin_0, R5.leg1, R5.wiper, J1.pin2
  DEL: R5.leg2

notes:
  Version 1
