# Fritzing sketch Neuron (saved by Fritzing 1.0.7)
breadboards: 1

parts:
  J1 = male pin header, 2 pins [form="♂ (male)"]
  R1 = Resistor [tolerance=±5% power=0.25W resistance=1k package=THT]
  P1 = male pin header, 2 pins [form="♂ (male)"]
  VR2 = 12mm Trimmer Potentiometer (Large) [maximum_resistance=10kΩ knob_status=50% power=0.5W package=THT]
  R3 = Resistor [tolerance=±5% power=0.25W resistance=1k package=THT]
  C1 = Electrolytic Capacitor [capacitance=100pF voltage=35V package="100 mil [THT, electrolytic]"]
  C3 = Electrolytic Capacitor [capacitance=100pF voltage=35V package="100 mil [THT, electrolytic]"]
  R2 = Resistor [tolerance=±5% power=0.25W resistance=1k package=THT]
  VR1 = 12mm Trimmer Potentiometer (Large) [maximum_resistance=10kΩ knob_status=50% power=0.5W package=THT]
  D1 = P0118MA 2AL3 [part_number="P0118MA 2AL3" package="TO-92 [THT]"]
  C2 = Electrolytic Capacitor [capacitance=100pF voltage=35V package="100 mil [THT, electrolytic]"]
  C4 = Electrolytic Capacitor [capacitance=100pF voltage=35V package="100 mil [THT, electrolytic]"]

nets:
  5V: J1.pin1, R1.Pin_0, C1.+, VR1.leg1, D1.A, C2.+
  GND: J1.pin2, P1.pin1, VR2.leg2, R3.Pin_0, C1.-, C3.-, C2.-, C4.-
  N1: R1.Pin_1, C3.+, R2.Pin_0, VR1.wiper, VR1.leg2, D1.K, D1.G, C4.+
  N2: P1.pin2, VR2.leg1, VR2.wiper, R3.Pin_1, R2.Pin_1

custom parts:
  P0118MA 2AL3: STMicroelectronics P0118MA sensitive high-immunity SCR (thyristor) in a TO-92 through-hole package. 600 V, 0.8 A RMS on-state current, very low gate trigger current (0.5-5 µA). Order code P0118MA 2AL3 (Ammopack). Pinout (flat face forward, leads down): pin1 Anode, pin2 Cathode, pin3 Gate.
