# Fritzing sketch Neuron_breadboard (saved by Fritzing 1.0.7)
breadboards: 1

parts:
  Rm = Resistor [tolerance=±5% power=0.25W resistance=680k package=THT]
  C1 = Ceramic Capacitor [capacitance=100nF voltage=35V package="100 mil [THT, multilayer]"]
  Ra = Resistor [tolerance=±5% power=0.25W resistance=2k package=THT]
  Thyristor = Thyristor [package="TO92 [THT]"]

nets (from the schematic view):
  N1: Rm.Pin_0, C1.1, Thyristor.K
  N2: Rm.Pin_1, Thyristor.A
  GND: C1.0, Ra.Pin_0
  V_ap: Ra.Pin_1, Thyristor.G
